# Fritzing sketch schematic_project1 (saved by Fritzing 0.9.3b)
circuit board: 6.89102cm x 5.4507cm
breadboards: 1

parts:
  S1 = Pushbutton [package="[SMD]"]
  S2 = Pushbutton [package="[SMD]"]
  S3 = Pushbutton [package="[SMD]"]
  LED1 = RGB LED - (4 legs) [package="5 mm [THT]"]
  Part1 = Arduino Uno (Rev3) - ICSP
  R6 = Resistor [tolerance=±5% resistance=1k package=THT]
  R2 = Resistor [tolerance=±5% resistance=10k package=THT]
  R1 = Resistor [tolerance=±5% resistance=10k package=THT]
  R5 = Resistor [tolerance=±5% resistance=1k package=THT]
  R4 = Resistor [tolerance=±5% resistance=330 package=THT]

nets:
  N1: S1.Pin_1, S1.Pin_2, Part1.ICSP_SCK, Part1.D13/SCK, R1.Pin_1
  N2: S1.Pin_3, S1.Pin_4, S2.Pin_3, S2.Pin_4, S3.Pin_3, S3.Pin_4, LED1.common_anode, Part1.GND
  N3: S2.Pin_1, S2.Pin_2, Part1.ICSP_MISO, Part1.D12/MISO, R2.Pin_1
  N4: S3.Pin_1, S3.Pin_2, Part1.ICSP_MOSI, Part1.D11_PWM/MOSI
  N5: LED1.red_cathode, R4.Pin_1
  N6: LED1.green_cathode, R5.Pin_1
  N7: LED1.blue_cathode, R6.Pin_1
  N8: Part1.5V, R2.Pin_0, R1.Pin_0
  N9: Part1.D3_PWM, R6.Pin_0
  N10: Part1.D4, R5.Pin_0
  N11: Part1.D5_PWM, R4.Pin_0
